# Fritzing sketch reed_sensor_design (saved by Fritzing 0.9.3b)
breadboards: 1

parts:
  S5 = Reed switch [package=THT]
  R1 = Resistor [tolerance=±5% resistance=220 package="0603 [SMD]"]
  U1 = NodeMCU V3.0

nets:
  N1: S5.pin_1, U1.GND
  N2: S5.pin_2, R1.Pin_0, U1.D2
  N3: R1.Pin_1, U1.3V3

custom parts:
  NodeMCU V3.0: ESP8266 based NodeMCU
